// Logisim project cpu.circ as structural Verilog: 10 circuits, main circuit main
module main (
);

  wire cpu_1_we, io_bus_node_1_we_out, io_bus_node_2_out_16, io_bus_node_2_we_out, io_bus_node_3_out_16,
       io_bus_node_3_we_out, io_bus_node_4_out_16, io_bus_node_4_we_out, io_bus_node_5_out_16,
       io_bus_node_5_we_out;
  wire [3:0] cpu_1_data_size, io_bus_node_2_out_17, io_bus_node_3_out_17, io_bus_node_4_out_9,
       io_bus_node_4_out_17, io_bus_node_5_out_9, io_bus_node_5_out_17;
  wire [6:0] bit_extender_1_out, keyboard_1_data;
  wire [7:0] io_bus_node_2_out_13, io_bus_node_3_out_13, io_bus_node_4_out_13, io_bus_node_5_out_13;
  wire [23:0] io_bus_node_1_address_out, io_bus_node_4_address_out, io_bus_node_5_address_out;
  wire [31:0] bit_extender_2_out, cpu_1_address, cpu_1_data_out, external_fpu_1_out_5, io_bus_node_1_data_in,
       io_bus_node_1_out_11, io_bus_node_2_data_in, io_bus_node_2_out_14, io_bus_node_2_out_15,
       io_bus_node_3_data_in, io_bus_node_3_out_11, io_bus_node_3_out_14, io_bus_node_3_out_15,
       io_bus_node_4_data_in, io_bus_node_4_out_11, io_bus_node_4_out_14, io_bus_node_4_out_15,
       io_bus_node_5_data_in, io_bus_node_5_out_11, io_bus_node_5_out_14, io_bus_node_5_out_15,
       ram_module_1_data_out, screen_driver_1_out_4, screen_driver_1_out_5, screen_driver_1_out_6,
       screen_driver_1_out_7, screen_driver_1_out_8, screen_driver_1_out_9, screen_driver_1_out_10,
       screen_driver_1_out_11, screen_driver_1_out_12, screen_driver_1_out_13, screen_driver_1_out_14,
       screen_driver_1_out_15, screen_driver_1_out_16, screen_driver_1_out_17, screen_driver_1_out_18,
       screen_driver_1_out_19, screen_driver_1_out_20, screen_driver_1_out_21, screen_driver_1_out_22,
       screen_driver_1_out_23, screen_driver_1_out_24, screen_driver_1_out_25, screen_driver_1_out_26,
       screen_driver_1_out_27, screen_driver_1_out_28, screen_driver_1_out_29, screen_driver_1_out_30,
       screen_driver_1_out_31, screen_driver_1_out_32, screen_driver_1_out_33, screen_driver_1_out_34,
       screen_driver_1_out_35;

  Bit_Extender #(.in_width(32), .out_width(7), .\type ("zero")) bit_extender_1 (
    .in(io_bus_node_3_out_11), .out(bit_extender_1_out));
  TTY tty_1 (.data(bit_extender_1_out), .clk(io_bus_node_3_we_out));  // open: we, clr
  Keyboard keyboard_1 (.clk(io_bus_node_2_we_out), .data(keyboard_1_data));  // open: re, clr, avail
  assign bit_extender_2_out = {{25{1'b0}}, keyboard_1_data};  // Bit_Extender bit_extender_2
  IO_bus_node io_bus_node_1 (
    .node_index(io_bus_node_2_out_13), .Address_in(io_bus_node_2_out_14), .Data_out(io_bus_node_2_out_15),
    .Data_in(io_bus_node_1_data_in), .WE(io_bus_node_2_out_16), .Data_size(io_bus_node_2_out_17),
    .WE_out(io_bus_node_1_we_out), .out_11(io_bus_node_1_out_11), .Address_out(io_bus_node_1_address_out));  // open: out_13, out_14, out_15, in_7, out_16, out_17, out_9, in_6
  IO_bus_node io_bus_node_2 (
    .node_index(io_bus_node_3_out_13), .Address_in(io_bus_node_3_out_14), .Data_out(io_bus_node_3_out_15),
    .Data_in(io_bus_node_2_data_in), .WE(io_bus_node_3_out_16), .Data_size(io_bus_node_3_out_17),
    .out_13(io_bus_node_2_out_13), .out_14(io_bus_node_2_out_14), .out_15(io_bus_node_2_out_15),
    .in_7(io_bus_node_1_data_in), .out_16(io_bus_node_2_out_16), .out_17(io_bus_node_2_out_17),
    .WE_out(io_bus_node_2_we_out), .in_6(bit_extender_2_out));  // open: out_9, out_11, Address_out
  IO_bus_node io_bus_node_3 (
    .node_index(io_bus_node_4_out_13), .Address_in(io_bus_node_4_out_14), .Data_out(io_bus_node_4_out_15),
    .Data_in(io_bus_node_3_data_in), .WE(io_bus_node_4_out_16), .Data_size(io_bus_node_4_out_17),
    .out_13(io_bus_node_3_out_13), .out_14(io_bus_node_3_out_14), .out_15(io_bus_node_3_out_15),
    .in_7(io_bus_node_2_data_in), .out_16(io_bus_node_3_out_16), .out_17(io_bus_node_3_out_17),
    .WE_out(io_bus_node_3_we_out), .out_11(io_bus_node_3_out_11));  // open: out_9, in_6, Address_out
  external_FPU external_fpu_1 (
    .in_1(io_bus_node_4_out_9), .in_2(io_bus_node_4_we_out), .out_5(external_fpu_1_out_5),
    .in_3(io_bus_node_4_out_11), .in_4(io_bus_node_4_address_out));
  IO_bus_node io_bus_node_4 (
    .node_index(io_bus_node_5_out_13), .Address_in(io_bus_node_5_out_14), .Data_out(io_bus_node_5_out_15),
    .Data_in(io_bus_node_4_data_in), .WE(io_bus_node_5_out_16), .Data_size(io_bus_node_5_out_17),
    .out_13(io_bus_node_4_out_13), .out_14(io_bus_node_4_out_14), .out_15(io_bus_node_4_out_15),
    .in_7(io_bus_node_3_data_in), .out_16(io_bus_node_4_out_16), .out_17(io_bus_node_4_out_17),
    .out_9(io_bus_node_4_out_9), .WE_out(io_bus_node_4_we_out), .in_6(external_fpu_1_out_5),
    .out_11(io_bus_node_4_out_11), .Address_out(io_bus_node_4_address_out));
  RAM_module ram_module_1 (
    .Adress(io_bus_node_5_address_out), .Data_in(io_bus_node_5_out_11), .Data_out(ram_module_1_data_out),
    .WE(io_bus_node_5_we_out), .Data_size(io_bus_node_5_out_9));
  IO_bus_node io_bus_node_5 (
    .Address_in(cpu_1_address), .Data_out(cpu_1_data_out), .Data_in(io_bus_node_5_data_in), .WE(cpu_1_we),
    .Data_size(cpu_1_data_size), .out_13(io_bus_node_5_out_13), .out_14(io_bus_node_5_out_14),
    .out_15(io_bus_node_5_out_15), .in_7(io_bus_node_4_data_in), .out_16(io_bus_node_5_out_16),
    .out_17(io_bus_node_5_out_17), .out_9(io_bus_node_5_out_9), .WE_out(io_bus_node_5_we_out),
    .in_6(ram_module_1_data_out), .out_11(io_bus_node_5_out_11), .Address_out(io_bus_node_5_address_out));  // open: node_index
  CPU cpu_1 (
    .Data_in(io_bus_node_5_data_in), .Data_size(cpu_1_data_size), .WE(cpu_1_we), .Data_out(cpu_1_data_out),
    .Address(cpu_1_address));
  // LedBar #(.inputtype("row"), .matrixcols(32)) ledbar_1: pin names not known; wires that end beside it: cpu_1_address
  // LedBar #(.inputtype("row"), .matrixcols(32)) ledbar_2: pin names not known; wires that end beside it: cpu_1_data_out
  // LedBar #(.inputtype("row"), .matrixcols(32)) ledbar_3: pin names not known; wires that end beside it: io_bus_node_5_data_in
  DotMatrix #(.inputtype("row"), .matrixcols(32), .matrixrows(32)) dotmatrix_1 (
    .row0(screen_driver_1_out_4), .row1(screen_driver_1_out_5), .row2(screen_driver_1_out_6),
    .row3(screen_driver_1_out_7), .row4(screen_driver_1_out_8), .row5(screen_driver_1_out_9),
    .row6(screen_driver_1_out_10), .row7(screen_driver_1_out_11), .row8(screen_driver_1_out_12),
    .row9(screen_driver_1_out_13), .row10(screen_driver_1_out_14), .row11(screen_driver_1_out_15),
    .row12(screen_driver_1_out_16), .row13(screen_driver_1_out_17), .row14(screen_driver_1_out_18),
    .row15(screen_driver_1_out_19), .row16(screen_driver_1_out_20), .row17(screen_driver_1_out_21),
    .row18(screen_driver_1_out_22), .row19(screen_driver_1_out_23), .row20(screen_driver_1_out_24),
    .row21(screen_driver_1_out_25), .row22(screen_driver_1_out_26), .row23(screen_driver_1_out_27),
    .row24(screen_driver_1_out_28), .row25(screen_driver_1_out_29), .row26(screen_driver_1_out_30),
    .row27(screen_driver_1_out_31), .row28(screen_driver_1_out_32), .row29(screen_driver_1_out_33),
    .row30(screen_driver_1_out_34), .row31(screen_driver_1_out_35));
  screen_driver screen_driver_1 (
    .in_1(io_bus_node_1_address_out), .in_2(io_bus_node_1_out_11), .in_3(io_bus_node_1_we_out),
    .out_4(screen_driver_1_out_4), .out_5(screen_driver_1_out_5), .out_6(screen_driver_1_out_6),
    .out_7(screen_driver_1_out_7), .out_8(screen_driver_1_out_8), .out_9(screen_driver_1_out_9),
    .out_10(screen_driver_1_out_10), .out_11(screen_driver_1_out_11), .out_12(screen_driver_1_out_12),
    .out_13(screen_driver_1_out_13), .out_14(screen_driver_1_out_14), .out_15(screen_driver_1_out_15),
    .out_16(screen_driver_1_out_16), .out_17(screen_driver_1_out_17), .out_18(screen_driver_1_out_18),
    .out_19(screen_driver_1_out_19), .out_20(screen_driver_1_out_20), .out_21(screen_driver_1_out_21),
    .out_22(screen_driver_1_out_22), .out_23(screen_driver_1_out_23), .out_24(screen_driver_1_out_24),
    .out_25(screen_driver_1_out_25), .out_26(screen_driver_1_out_26), .out_27(screen_driver_1_out_27),
    .out_28(screen_driver_1_out_28), .out_29(screen_driver_1_out_29), .out_30(screen_driver_1_out_30),
    .out_31(screen_driver_1_out_31), .out_32(screen_driver_1_out_32), .out_33(screen_driver_1_out_33),
    .out_34(screen_driver_1_out_34), .out_35(screen_driver_1_out_35));
endmodule

module CPU (
  input  [31:0] Data_in,
  output [3:0] Data_size,
  output WE,
  output [31:0] Data_out,
  output [31:0] Address
);

  wire and_1_out, and_3_out, and_4_out, clock_1_out, decode_1_mem_access, decode_1_regstr,
       decode_1_should_branch, decoder_1_out0, decoder_1_out1, decoder_1_out2, decoder_1_out3,
       decoder_2_out4, decoder_2_out5, decoder_2_out6, decoder_2_out7, decoder_2_out9, decoder_3_out1,
       decoder_3_out2, decoder_3_out3, or_1_out, or_2_out;
  wire [1:0] counter_1_q;
  wire [2:0] decode_1_funct3;
  wire [3:0] decode_1_inst_type, decode_1_mem_enable;
  wire [4:0] decode_1_rd, decode_1_rs1, decode_1_rs2;
  wire [6:0] decode_1_funct7;
  wire [31:0] adder_1_out, adder_2_out, adder_3_out, alu_1_out_5, decode_1_address, decode_1_data_out,
       multiplexer_1_out, multiplexer_2_out, multiplexer_5_out, register_1_q, register_2_q, register_3_q,
       regs_1_s1;

  and and_1 (and_1_out, decode_1_should_branch, decoder_2_out5);
  or or_1 (or_1_out, and_1_out, decoder_2_out6, decoder_2_out9);
  Adder #(.width(32)) adder_1 (.a(register_1_q), .b(32'h4), .out(adder_1_out));  // open: cin, cout
  Adder #(.width(32)) adder_2 (.a(decode_1_data_out), .b(register_1_q), .out(adder_2_out));  // open: cin, cout
  Clock clock_1 (.out(clock_1_out));
  Multiplexer #(.width(32)) multiplexer_1 (
    .in0(adder_1_out), .in1(adder_2_out), .out(multiplexer_1_out), .sel(or_1_out));
  Multiplexer #(.width(32)) multiplexer_2 (
    .in0(multiplexer_1_out), .in1(adder_3_out), .out(multiplexer_2_out), .sel(decoder_2_out7));
  Decoder #(.select(2)) decoder_1 (
    .out0(decoder_1_out0), .out1(decoder_1_out1), .out2(decoder_1_out2), .out3(decoder_1_out3),
    .sel(counter_1_q), .en(clock_1_out));
  Counter #(.max('h3), .trigger("falling"), .width(2)) counter_1 (
    .Q(counter_1_q), .clk(clock_1_out));  // open: load, D, count, carry, up, clr
  Decoder #(.select(4)) decoder_2 (
    .out4(decoder_2_out4), .out5(decoder_2_out5), .out6(decoder_2_out6), .out7(decoder_2_out7),
    .out9(decoder_2_out9), .sel(decode_1_inst_type));  // open: out0, out1, out2, out3, out8, out10, out11, out12, out13, out14, out15, en
  Register #(.trigger("falling"), .width(32)) register_1 (
    .D(multiplexer_2_out), .Q(register_1_q), .clk(decoder_1_out2));  // open: en, clr
  Multiplexer #(.width(32)) multiplexer_3 (.in0(register_1_q), .in1(decode_1_address), .out(Address), .sel(and_3_out));
  and and_2 (WE, decoder_2_out4, decoder_1_out1);
  Register #(.width(32)) register_2 (.D(adder_1_out), .Q(register_2_q), .clk(decoder_1_out2));  // open: en, clr
  and and_3 (and_3_out, or_2_out, decode_1_mem_access);
  or or_2 (or_2_out, decoder_3_out1, decoder_3_out2, decoder_3_out3);
  Decoder #(.select(2)) decoder_3 (
    .out1(decoder_3_out1), .out2(decoder_3_out2), .out3(decoder_3_out3), .sel(counter_1_q));  // open: out0, en
  Multiplexer #(.width(4)) multiplexer_4 (.in0(4'b1111), .in1(decode_1_mem_enable), .out(Data_size), .sel(and_3_out));
  Register #(.width(32)) register_3 (.D(Data_in), .Q(register_3_q), .clk(decoder_1_out0));  // open: en, clr
  Pull_Resistor pull_resistor_1 (.node(register_3_q));
  and and_4 (and_4_out, decoder_1_out3, decode_1_regstr);
  Multiplexer #(.select(4), .width(32)) multiplexer_5 (
    .in1(alu_1_out_5), .in2(alu_1_out_5), .in3(Data_in), .in4(Data_in), .in6(register_2_q),
    .in7(register_2_q), .in8(decode_1_data_out), .out(multiplexer_5_out), .sel(decode_1_inst_type));  // open: in0, in5, in9, in10, in11, in12, in13, in14, in15
  regs regs_1 (
    .reg_save(and_4_out), .rd(decode_1_rd), .rs1(decode_1_rs1), .rs2(decode_1_rs2),
    .data_in(multiplexer_5_out), .s1(regs_1_s1), .s2(Data_out));
  decode decode_1 (
    .in_1(register_3_q), .s1(regs_1_s1), .s2(Data_out), .PC(register_1_q), .inst_type(decode_1_inst_type),
    .regStr(decode_1_regstr), .rd(decode_1_rd), .rs1(decode_1_rs1), .rs2(decode_1_rs2),
    .funct3(decode_1_funct3), .funct7(decode_1_funct7), .Data_out(decode_1_data_out),
    .should_branch(decode_1_should_branch), .mem_enable(decode_1_mem_enable), .Address(decode_1_address),
    .mem_access(decode_1_mem_access));
  Adder #(.width(32)) adder_3 (.a(decode_1_data_out), .b(regs_1_s1), .out(adder_3_out));  // open: cin, cout
  ALU alu_1 (
    .funct3(decode_1_funct3), .A(regs_1_s1), .B(decode_1_data_out), .funct7(decode_1_funct7),
    .out_5(alu_1_out_5));
endmodule

module ALU (
  input  [31:0] A,
  input  [31:0] B,
  input  [2:0] funct3,
  input  [6:0] funct7,
  output [31:0] out_5
);

  wire comparator_1_lt, comparator_2_lt;
  wire [4:0] bit_extender_2_out, bit_extender_5_out;
  wire [31:0] adder_1_out, and_1_out, bit_extender_1_out, bit_extender_6_out, bit_extender_7_out,
       divider_1_out, divider_1_rem, divider_2_out, divider_2_rem, multiplexer_1_out, multiplexer_2_out,
       multiplexer_3_out, multiplier_2_cout, multiplier_3_cout, multiplier_3_out, or_1_out, shifter_1_out,
       shifter_2_out, shifter_3_out, xor_1_out, xor_2_out;
  wire [63:0] bit_extender_3_out, bit_extender_4_out, multiplier_1_out;

  assign bit_extender_1_out = {{31{funct7[5]}}, funct7[5]};  // Bit_Extender bit_extender_1
  Bit_Extender #(.in_width(32), .out_width(5), .\type ("zero")) bit_extender_2 (.in(B), .out(bit_extender_2_out));
  assign bit_extender_3_out = {{32{A[31]}}, A};  // Bit_Extender bit_extender_3
  Multiplier #(.mode("twosComplement"), .width(64)) multiplier_1 (
    .a(bit_extender_3_out), .b(bit_extender_4_out), .out(multiplier_1_out));  // open: cin, cout
  assign bit_extender_4_out = {{32{1'b0}}, B};  // Bit_Extender bit_extender_4
  Multiplier #(.mode("twosComplement"), .width(32)) multiplier_2 (
    .a(A), .b(B), .cout(multiplier_2_cout));  // open: out, cin
  Divider #(.mode("twosComplement"), .width(32)) divider_1 (
    .a(A), .b(B), .out(divider_1_out), .rem(divider_1_rem));  // open: upper
  Divider #(.width(32)) divider_2 (.a(A), .b(B), .out(divider_2_out), .rem(divider_2_rem));  // open: upper
  Adder #(.width(32)) adder_1 (.a(A), .b(xor_1_out), .out(adder_1_out), .cin(funct7[5]));  // open: cout
  assign xor_1_out = B ^ bit_extender_1_out;  // XOR_Gate xor_1, 32 bits wide
  Shifter #(.width(32)) shifter_1 (.in(A), .\dist (bit_extender_5_out), .out(shifter_1_out));
  Bit_Extender #(.in_width(32), .out_width(5), .\type ("zero")) bit_extender_5 (.in(B), .out(bit_extender_5_out));
  assign bit_extender_6_out = {{31{1'b0}}, comparator_1_lt};  // Bit_Extender bit_extender_6
  Comparator #(.width(32)) comparator_1 (.a(A), .b(B), .lt(comparator_1_lt));  // open: gt, eq
  assign bit_extender_7_out = {{31{1'b0}}, comparator_2_lt};  // Bit_Extender bit_extender_7
  Comparator #(.mode("unsigned"), .width(32)) comparator_2 (.a(A), .b(B), .lt(comparator_2_lt));  // open: gt, eq
  assign xor_2_out = A ^ B;  // XOR_Gate xor_2, 32 bits wide
  Shifter #(.shift("lr"), .width(32)) shifter_2 (.in(A), .\dist (bit_extender_2_out), .out(shifter_2_out));
  Multiplexer #(.width(32)) multiplexer_1 (
    .in0(shifter_2_out), .in1(shifter_3_out), .out(multiplexer_1_out), .sel(funct7[5]));
  Shifter #(.shift("ar"), .width(32)) shifter_3 (.in(A), .\dist (bit_extender_2_out), .out(shifter_3_out));
  assign or_1_out = A | B;  // OR_Gate or_1, 32 bits wide
  assign and_1_out = A & B;  // AND_Gate and_1, 32 bits wide
  Multiplier #(.mode("twosComplement"), .width(32)) multiplier_3 (
    .a(A), .b(B), .out(multiplier_3_out), .cout(multiplier_3_cout));  // open: cin
  Multiplexer #(.select(3), .width(32)) multiplexer_2 (
    .in0(adder_1_out), .in1(shifter_1_out), .in2(bit_extender_6_out), .in3(bit_extender_7_out),
    .in4(xor_2_out), .in5(multiplexer_1_out), .in6(or_1_out), .in7(and_1_out), .out(multiplexer_2_out),
    .sel(funct3));
  Multiplexer #(.select(3), .width(32)) multiplexer_3 (
    .in0(multiplier_3_out), .in1(multiplier_3_cout), .in2(multiplier_1_out[63:32]), .in3(multiplier_2_cout),
    .in4(divider_1_out), .in5(divider_2_out), .in6(divider_1_rem), .in7(divider_2_rem),
    .out(multiplexer_3_out), .sel(funct3));
  Multiplexer #(.width(32)) multiplexer_4 (
    .in0(multiplexer_2_out), .in1(multiplexer_3_out), .out(out_5), .sel(funct7[0]));
endmodule

module decode (
  input  [31:0] in_1,
  input  [31:0] s1,
  input  [31:0] s2,
  input  [31:0] PC,
  output [3:0] inst_type,
  output regStr,
  output [4:0] rd,
  output [4:0] rs1,
  output [4:0] rs2,
  output [2:0] funct3,
  output [6:0] funct7,
  output [31:0] Data_out,
  output should_branch,
  output [3:0] mem_enable,
  output [31:0] Address,
  output mem_access
);

  wire and_1_out, comparator_1_eq, comparator_1_gt, comparator_1_lt, comparator_2_eq, comparator_2_gt,
       comparator_2_lt, not_1_out, opdecoder_1_alu, opdecoder_1_aluimm, opdecoder_1_auipc,
       opdecoder_1_branch, opdecoder_1_dunno, opdecoder_1_jal, opdecoder_1_jalr, opdecoder_1_load,
       opdecoder_1_lui, opdecoder_1_store, or_2_out, or_3_out, or_4_out, priority_encoder_1_p10;
  wire [31:0] adder_1_out, bit_extender_1_out, bit_extender_2_out, bit_extender_3_out, bit_extender_4_out,
       bit_extender_5_out, bit_extender_6_out, bit_extender_7_out, bit_extender_8_out, bit_extender_9_out,
       multiplexer_1_out, multiplexer_2_out, multiplexer_3_out, multiplexer_4_out, pull_resistor_2_node;

  opDecoder opdecoder_1 (
    .in_1(in_1[6:0]), .ALU(opdecoder_1_alu), .ALUimm(opdecoder_1_aluimm), .load(opdecoder_1_load),
    .store(opdecoder_1_store), .branch(opdecoder_1_branch), .jal(opdecoder_1_jal), .jalr(opdecoder_1_jalr),
    .lui(opdecoder_1_lui), .auipc(opdecoder_1_auipc), .dunno(opdecoder_1_dunno));
  assign bit_extender_1_out = {{24{in_1[7]}}, in_1[7:0]};  // Bit_Extender bit_extender_1
  assign bit_extender_2_out = {{24{1'b0}}, in_1[7:0]};  // Bit_Extender bit_extender_2
  assign bit_extender_3_out = {{16{in_1[15]}}, in_1[15:0]};  // Bit_Extender bit_extender_3
  assign bit_extender_4_out = {{16{1'b0}}, in_1[15:0]};  // Bit_Extender bit_extender_4
  or or_1 (regStr, opdecoder_1_alu, opdecoder_1_aluimm, opdecoder_1_load, opdecoder_1_jal, opdecoder_1_jalr, opdecoder_1_lui, opdecoder_1_auipc, opdecoder_1_dunno);
  Multiplexer #(.width(32)) multiplexer_1 (
    .in0(bit_extender_1_out), .in1(bit_extender_2_out), .out(multiplexer_1_out), .sel(in_1[14]));
  Multiplexer #(.width(32)) multiplexer_2 (
    .in0(bit_extender_3_out), .in1(bit_extender_4_out), .out(multiplexer_2_out), .sel(in_1[14]));
  not not_1 (not_1_out, opdecoder_1_aluimm);
  assign funct7 = not_1_out ? in_1[31:25] : 7'bz;  // Controlled_Buffer controlled_buffer_1
  and and_1 (and_1_out, opdecoder_1_load, in_1[12], ~in_1[13], 1'b1);  // AND_Gate
  assign bit_extender_5_out = {{20{in_1[31]}}, in_1[31:20]};  // Bit_Extender bit_extender_5
  Multiplexer #(.width(32)) multiplexer_3 (
    .in0(bit_extender_5_out), .in1(bit_extender_6_out), .out(multiplexer_3_out), .sel(and_1_out));
  assign bit_extender_6_out = {{20{1'b0}}, in_1[31:20]};  // Bit_Extender bit_extender_6
  assign bit_extender_7_out = {{20{in_1[31]}}, {in_1[31:25], in_1[11:7]}};  // Bit_Extender bit_extender_7
  assign bit_extender_8_out = {{19{in_1[31]}}, {in_1[31], in_1[7], in_1[30:25], in_1[11:8], 1'b0}};  // Bit_Extender bit_extender_8
  assign bit_extender_9_out = {{11{in_1[31]}}, {in_1[31], in_1[19:12], in_1[20], in_1[30:21], 1'b0}};  // Bit_Extender bit_extender_9
  Multiplexer #(.select(2), .width(32)) multiplexer_4 (
    .in0(multiplexer_1_out), .in1(multiplexer_2_out), .in2(in_1), .out(multiplexer_4_out), .sel(in_1[13:12]));  // open: in3
  Pull_Resistor pull_resistor_1 (.node(funct7));
  Comparator #(.width(32)) comparator_1 (
    .a(s1), .b(s2), .gt(comparator_1_gt), .eq(comparator_1_eq), .lt(comparator_1_lt));
  Comparator #(.width(32)) comparator_2 (
    .a(s1), .b(s2), .gt(comparator_2_gt), .eq(comparator_2_eq), .lt(comparator_2_lt));
  // Priority_Encoder #(.select(4)) priority_encoder_1: pin names not known; wires that end beside it: opdecoder_1_alu, opdecoder_1_aluimm, opdecoder_1_load, opdecoder_1_store, opdecoder_1_branch, opdecoder_1_jal, opdecoder_1_jalr, inst_type, opdecoder_1_lui, priority_encoder_1_p10, opdecoder_1_auipc, opdecoder_1_dunno
  Adder #(.width(32)) adder_1 (.a({in_1[31:12], {12{1'b0}}}), .b(PC), .out(adder_1_out));  // open: cin, cout
  or or_2 (or_2_out, comparator_1_gt, comparator_1_lt);
  or or_3 (or_3_out, comparator_1_gt, comparator_1_eq);
  or or_4 (or_4_out, comparator_2_eq, comparator_2_gt);
  or or_5 (mem_access, opdecoder_1_load, opdecoder_1_store);
  Multiplexer #(.enable("true"), .select(4), .width(32)) multiplexer_5 (
    .in1(s2), .in2(multiplexer_3_out), .in3(multiplexer_4_out), .in5(bit_extender_8_out),
    .in6(bit_extender_9_out), .in7(multiplexer_3_out), .in8({in_1[31:12], {12{1'b0}}}), .in9(adder_1_out),
    .in10(multiplexer_3_out), .out(Data_out), .sel(inst_type), .en(priority_encoder_1_p10));  // open: in0, in4, in11, in12, in13, in14, in15
  Pull_Resistor pull_resistor_2 (.node(pull_resistor_2_node));
  Multiplexer #(.enable("true"), .select(4), .width(32)) multiplexer_6 (
    .in3(multiplexer_3_out), .in4(bit_extender_7_out), .out(pull_resistor_2_node), .sel(inst_type));  // open: in0, in1, in2, in5, in6, in7, in8, in9, in10, in11, in12, in13, in14, in15, en
  Multiplexer #(.select(3)) multiplexer_7 (
    .in0(comparator_1_eq), .in1(or_2_out), .in4(comparator_1_lt), .in5(or_3_out), .in6(comparator_2_lt),
    .in7(or_4_out), .out(should_branch), .sel(in_1[14:12]));  // open: in2, in3
  Pull_Resistor pull_resistor_3 (.node(inst_type));
  Pull_Resistor pull_resistor_4 (.node(Data_out));
  Adder #(.width(32)) adder_2 (.a(pull_resistor_2_node), .b(s1), .out(Address));  // open: cin, cout
  or or_6 (mem_enable[1], in_1[12], in_1[13]);

  assign funct3 = in_1[14:12];
  assign {mem_enable[3:2], mem_enable[0]} = {{2{in_1[13]}}, 1'b1};
  assign rd = in_1[11:7];
  assign rs1 = in_1[19:15];
  assign rs2 = in_1[24:20];
endmodule

module opDecoder (
  input  [6:0] in_1,
  output ALU,
  output ALUimm,
  output load,
  output store,
  output branch,
  output jal,
  output jalr,
  output lui,
  output auipc,
  output dunno
);

  and and_1 (ALU, in_1[0], in_1[1], ~in_1[2], ~in_1[3], in_1[4], in_1[5], ~in_1[6]);  // AND_Gate
  and and_2 (ALUimm, in_1[0], in_1[1], ~in_1[2], ~in_1[3], in_1[4], ~in_1[5], ~in_1[6]);  // AND_Gate
  and and_3 (load, in_1[0], in_1[1], ~in_1[2], ~in_1[3], ~in_1[4], ~in_1[5], ~in_1[6]);  // AND_Gate
  and and_4 (store, in_1[0], in_1[1], ~in_1[2], ~in_1[3], ~in_1[4], in_1[5], ~in_1[6]);  // AND_Gate
  and and_5 (branch, in_1[0], in_1[1], ~in_1[2], ~in_1[3], ~in_1[4], in_1[5], in_1[6]);  // AND_Gate
  and and_6 (jal, in_1[0], in_1[1], in_1[2], in_1[3], ~in_1[4], in_1[5], in_1[6]);  // AND_Gate
  and and_7 (jalr, in_1[0], in_1[1], in_1[2], ~in_1[3], ~in_1[4], in_1[5], in_1[6]);  // AND_Gate
  and and_8 (lui, in_1[0], in_1[1], in_1[2], ~in_1[3], in_1[4], in_1[5], ~in_1[6]);  // AND_Gate
  and and_9 (auipc, in_1[0], in_1[1], in_1[2], ~in_1[3], in_1[4], ~in_1[5], ~in_1[6]);  // AND_Gate
  and and_10 (dunno, in_1[0], in_1[1], ~in_1[2], ~in_1[3], in_1[4], in_1[5], in_1[6]);  // AND_Gate
endmodule

module regs (
  input  reg_save,
  input  [4:0] rd,
  input  [4:0] rs1,
  input  [4:0] rs2,
  input  [31:0] data_in,
  output [31:0] s1,
  output [31:0] s2
);

  wire decoder_1_out1, decoder_1_out2, decoder_1_out3, decoder_1_out4, decoder_1_out5, decoder_1_out6,
       decoder_1_out7, decoder_1_out8, decoder_1_out9, decoder_1_out10, decoder_1_out11, decoder_1_out12,
       decoder_1_out13, decoder_1_out14, decoder_1_out15, decoder_1_out16, decoder_1_out17, decoder_1_out18,
       decoder_1_out19, decoder_1_out20, decoder_1_out21, decoder_1_out22, decoder_1_out23, decoder_1_out24,
       decoder_1_out25, decoder_1_out26, decoder_1_out27, decoder_1_out28, decoder_1_out29, decoder_1_out30,
       decoder_1_out31;
  wire [31:0] register_1_q, register_2_q, register_3_q, register_4_q, register_5_q, register_6_q,
       register_7_q, register_8_q, register_9_q, register_10_q, register_11_q, register_12_q, register_13_q,
       register_14_q, register_15_q, register_16_q, register_17_q, register_18_q, register_19_q,
       register_20_q, register_21_q, register_22_q, register_23_q, register_24_q, register_25_q,
       register_26_q, register_27_q, register_28_q, register_29_q, register_30_q, register_31_q;

  Decoder #(.select(5)) decoder_1 (
    .out1(decoder_1_out1), .out2(decoder_1_out2), .out3(decoder_1_out3), .out4(decoder_1_out4),
    .out5(decoder_1_out5), .out6(decoder_1_out6), .out7(decoder_1_out7), .out8(decoder_1_out8),
    .out9(decoder_1_out9), .out10(decoder_1_out10), .out11(decoder_1_out11), .out12(decoder_1_out12),
    .out13(decoder_1_out13), .out14(decoder_1_out14), .out15(decoder_1_out15), .out16(decoder_1_out16),
    .out17(decoder_1_out17), .out18(decoder_1_out18), .out19(decoder_1_out19), .out20(decoder_1_out20),
    .out21(decoder_1_out21), .out22(decoder_1_out22), .out23(decoder_1_out23), .out24(decoder_1_out24),
    .out25(decoder_1_out25), .out26(decoder_1_out26), .out27(decoder_1_out27), .out28(decoder_1_out28),
    .out29(decoder_1_out29), .out30(decoder_1_out30), .out31(decoder_1_out31), .sel(rd), .en(reg_save));  // open: out0
  Register #(.trigger("falling"), .width(32)) register_1 (
    .D(data_in), .Q(register_1_q), .clk(decoder_1_out1));  // open: en, clr
  Register #(.trigger("falling"), .width(32)) register_2 (
    .D(data_in), .Q(register_2_q), .clk(decoder_1_out2));  // open: en, clr
  Register #(.trigger("falling"), .width(32)) register_3 (
    .D(data_in), .Q(register_3_q), .clk(decoder_1_out3));  // open: en, clr
  Register #(.trigger("falling"), .width(32)) register_4 (
    .D(data_in), .Q(register_4_q), .clk(decoder_1_out4));  // open: en, clr
  Register #(.trigger("falling"), .width(32)) register_5 (
    .D(data_in), .Q(register_5_q), .clk(decoder_1_out5));  // open: en, clr
  Register #(.trigger("falling"), .width(32)) register_6 (
    .D(data_in), .Q(register_6_q), .clk(decoder_1_out6));  // open: en, clr
  Register #(.trigger("falling"), .width(32)) register_7 (
    .D(data_in), .Q(register_7_q), .clk(decoder_1_out7));  // open: en, clr
  Register #(.trigger("falling"), .width(32)) register_8 (
    .D(data_in), .Q(register_8_q), .clk(decoder_1_out8));  // open: en, clr
  Register #(.trigger("falling"), .width(32)) register_9 (
    .D(data_in), .Q(register_9_q), .clk(decoder_1_out9));  // open: en, clr
  Register #(.trigger("falling"), .width(32)) register_10 (
    .D(data_in), .Q(register_10_q), .clk(decoder_1_out10));  // open: en, clr
  Register #(.trigger("falling"), .width(32)) register_11 (
    .D(data_in), .Q(register_11_q), .clk(decoder_1_out11));  // open: en, clr
  Register #(.trigger("falling"), .width(32)) register_12 (
    .D(data_in), .Q(register_12_q), .clk(decoder_1_out12));  // open: en, clr
  Register #(.trigger("falling"), .width(32)) register_13 (
    .D(data_in), .Q(register_13_q), .clk(decoder_1_out13));  // open: en, clr
  Register #(.trigger("falling"), .width(32)) register_14 (
    .D(data_in), .Q(register_14_q), .clk(decoder_1_out14));  // open: en, clr
  Register #(.trigger("falling"), .width(32)) register_15 (
    .D(data_in), .Q(register_15_q), .clk(decoder_1_out15));  // open: en, clr
  Register #(.trigger("falling"), .width(32)) register_16 (
    .D(data_in), .Q(register_16_q), .clk(decoder_1_out16));  // open: en, clr
  Register #(.trigger("falling"), .width(32)) register_17 (
    .D(data_in), .Q(register_17_q), .clk(decoder_1_out17));  // open: en, clr
  Register #(.trigger("falling"), .width(32)) register_18 (
    .D(data_in), .Q(register_18_q), .clk(decoder_1_out18));  // open: en, clr
  Register #(.trigger("falling"), .width(32)) register_19 (
    .D(data_in), .Q(register_19_q), .clk(decoder_1_out19));  // open: en, clr
  Register #(.trigger("falling"), .width(32)) register_20 (
    .D(data_in), .Q(register_20_q), .clk(decoder_1_out20));  // open: en, clr
  Register #(.trigger("falling"), .width(32)) register_21 (
    .D(data_in), .Q(register_21_q), .clk(decoder_1_out21));  // open: en, clr
  Register #(.trigger("falling"), .width(32)) register_22 (
    .D(data_in), .Q(register_22_q), .clk(decoder_1_out22));  // open: en, clr
  Register #(.trigger("falling"), .width(32)) register_23 (
    .D(data_in), .Q(register_23_q), .clk(decoder_1_out23));  // open: en, clr
  Register #(.trigger("falling"), .width(32)) register_24 (
    .D(data_in), .Q(register_24_q), .clk(decoder_1_out24));  // open: en, clr
  Register #(.trigger("falling"), .width(32)) register_25 (
    .D(data_in), .Q(register_25_q), .clk(decoder_1_out25));  // open: en, clr
  Register #(.trigger("falling"), .width(32)) register_26 (
    .D(data_in), .Q(register_26_q), .clk(decoder_1_out26));  // open: en, clr
  Register #(.trigger("falling"), .width(32)) register_27 (
    .D(data_in), .Q(register_27_q), .clk(decoder_1_out27));  // open: en, clr
  Register #(.trigger("falling"), .width(32)) register_28 (
    .D(data_in), .Q(register_28_q), .clk(decoder_1_out28));  // open: en, clr
  Register #(.trigger("falling"), .width(32)) register_29 (
    .D(data_in), .Q(register_29_q), .clk(decoder_1_out29));  // open: en, clr
  Register #(.trigger("falling"), .width(32)) register_30 (
    .D(data_in), .Q(register_30_q), .clk(decoder_1_out30));  // open: en, clr
  Register #(.trigger("falling"), .width(32)) register_31 (
    .D(data_in), .Q(register_31_q), .clk(decoder_1_out31));  // open: en, clr
  Multiplexer #(.select(5), .width(32)) multiplexer_1 (
    .in0({32{1'b0}}), .in1(register_1_q), .in2(register_2_q), .in3(register_3_q), .in4(register_4_q),
    .in5(register_5_q), .in6(register_6_q), .in7(register_7_q), .in8(register_8_q), .in9(register_9_q),
    .in10(register_10_q), .in11(register_11_q), .in12(register_12_q), .in13(register_13_q),
    .in14(register_14_q), .in15(register_15_q), .in16(register_16_q), .in17(register_17_q),
    .in18(register_18_q), .in19(register_19_q), .in20(register_20_q), .in21(register_21_q),
    .in22(register_22_q), .in23(register_23_q), .in24(register_24_q), .in25(register_25_q),
    .in26(register_26_q), .in27(register_27_q), .in28(register_28_q), .in29(register_29_q),
    .in30(register_30_q), .in31(register_31_q), .out(s1), .sel(rs1));
  Multiplexer #(.select(5), .width(32)) multiplexer_2 (
    .in0({32{1'b0}}), .in1(register_1_q), .in2(register_2_q), .in3(register_3_q), .in4(register_4_q),
    .in5(register_5_q), .in6(register_6_q), .in7(register_7_q), .in8(register_8_q), .in9(register_9_q),
    .in10(register_10_q), .in11(register_11_q), .in12(register_12_q), .in13(register_13_q),
    .in14(register_14_q), .in15(register_15_q), .in16(register_16_q), .in17(register_17_q),
    .in18(register_18_q), .in19(register_19_q), .in20(register_20_q), .in21(register_21_q),
    .in22(register_22_q), .in23(register_23_q), .in24(register_24_q), .in25(register_25_q),
    .in26(register_26_q), .in27(register_27_q), .in28(register_28_q), .in29(register_29_q),
    .in30(register_30_q), .in31(register_31_q), .out(s2), .sel(rs2));
endmodule

module RAM_module (
  input  [23:0] Adress,
  input  [31:0] Data_in,
  input  WE,
  input  [3:0] Data_size,
  output [31:0] Data_out
);

  wire [7:0] ram_1_p4, ram_1_p5, ram_1_p6, ram_1_p7;

  // RAM #(.addrWidth(24), .enables("line"), .line("quad"), .misaligned("true"), .\type ("nonvolatile")) ram_1: pin names not known; wires that end beside it: Adress, WE, WE, ram_1_p4, ram_1_p5, ram_1_p6, ram_1_p7
  assign Data_out[15:8] = Data_size[1] ? ram_1_p5 : 8'bz;  // Controlled_Buffer controlled_buffer_1
  assign Data_out[23:16] = Data_size[2] ? ram_1_p6 : 8'bz;  // Controlled_Buffer controlled_buffer_2
  assign Data_out[31:24] = Data_size[3] ? ram_1_p7 : 8'bz;  // Controlled_Buffer controlled_buffer_3
  Pull_Resistor pull_resistor_1 (.node(Data_out));
  assign Data_out[7:0] = Data_size[0] ? ram_1_p4 : 8'bz;  // Controlled_Buffer controlled_buffer_4
endmodule

module external_FPU (
  input  [3:0] in_1,
  input  in_2,
  input  [31:0] in_3,
  input  [23:0] in_4,
  output [31:0] out_5
);

  wire demultiplexer_1_out0, demultiplexer_1_out1, demultiplexer_1_out2, fpcomparator_1_p3,
       fpcomparator_1_p4, fpcomparator_1_p5;
  wire [3:0] bit_extender_4_out;
  wire [31:0] bit_extender_1_out, bit_extender_2_out, bit_extender_3_out, demultiplexer_2_out0,
       demultiplexer_2_out1, demultiplexer_2_out2, fpadder_1_out, fpdivider_1_out, fpmultiplier_1_out,
       fpnegator_1_p2, fpsubtractor_1_out, fptoint_1_p2, inttofp_1_p2, multiplexer_2_out, register_1_q,
       register_2_q, register_3_q;

  Pull_Resistor pull_resistor_1 (.node(out_5));
  Demultiplexer #(.select(2)) demultiplexer_1 (
    .out0(demultiplexer_1_out0), .out1(demultiplexer_1_out1), .out2(demultiplexer_1_out2), .in(in_2),
    .sel(in_4[1:0]));  // open: out3
  Demultiplexer #(.select(2), .width(32)) demultiplexer_2 (
    .out0(demultiplexer_2_out0), .out1(demultiplexer_2_out1), .out2(demultiplexer_2_out2), .in(in_3),
    .sel(in_4[1:0]));  // open: out3
  Multiplexer #(.select(2), .width(32)) multiplexer_1 (
    .in3(multiplexer_2_out), .out(out_5), .sel(in_4[1:0]));  // open: in0, in1, in2
  Register #(.width(32)) register_1 (
    .D(demultiplexer_2_out0), .Q(register_1_q), .clk(demultiplexer_1_out0));  // open: en, clr
  Register #(.width(32)) register_2 (
    .D(demultiplexer_2_out1), .Q(register_2_q), .clk(demultiplexer_1_out1));  // open: en, clr
  Register #(.width(32)) register_3 (
    .D(demultiplexer_2_out2), .Q(register_3_q), .clk(demultiplexer_1_out2));  // open: en, clr
  FPAdder fpadder_1 (.a(register_2_q), .b(register_1_q), .out(fpadder_1_out));
  FPSubtractor fpsubtractor_1 (.a(register_2_q), .b(register_1_q), .out(fpsubtractor_1_out));
  FPMultiplier fpmultiplier_1 (.a(register_2_q), .b(register_1_q), .out(fpmultiplier_1_out));
  FPDivider fpdivider_1 (.a(register_2_q), .b(register_1_q), .out(fpdivider_1_out));
  // FPNegator fpnegator_1: pin names not known; wires that end beside it: register_1_q, fpnegator_1_p2
  // FPComparator fpcomparator_1: pin names not known; wires that end beside it: register_2_q, register_1_q, fpcomparator_1_p3, fpcomparator_1_p4, fpcomparator_1_p5
  // FPToInt #(.width(32)) fptoint_1: pin names not known; wires that end beside it: register_1_q, fptoint_1_p2
  // IntToFP #(.width(32)) inttofp_1: pin names not known; wires that end beside it: register_1_q, inttofp_1_p2
  assign bit_extender_1_out = {{31{1'b0}}, fpcomparator_1_p3};  // Bit_Extender bit_extender_1
  assign bit_extender_2_out = {{31{1'b0}}, fpcomparator_1_p4};  // Bit_Extender bit_extender_2
  assign bit_extender_3_out = {{31{1'b0}}, fpcomparator_1_p5};  // Bit_Extender bit_extender_3
  Bit_Extender #(.in_width(32), .out_width(4), .\type ("zero")) bit_extender_4 (
    .in(register_3_q), .out(bit_extender_4_out));
  Multiplexer #(.select(4), .width(32)) multiplexer_2 (
    .in0(fpadder_1_out), .in1(fpsubtractor_1_out), .in2(fpmultiplier_1_out), .in3(fpdivider_1_out),
    .in4(fpnegator_1_p2), .in5(bit_extender_1_out), .in6(bit_extender_2_out), .in7(bit_extender_3_out),
    .in8(fptoint_1_p2), .in9(inttofp_1_p2), .out(multiplexer_2_out), .sel(bit_extender_4_out));  // open: in10, in11, in12, in13, in14, in15
endmodule

module IO_bus_node (
  input  [7:0] node_index,
  input  [31:0] Address_in,
  input  [31:0] Data_out,
  input  WE,
  input  [3:0] Data_size,
  input  [31:0] in_6,
  input  [31:0] in_7,
  output [31:0] Data_in,
  output [3:0] out_9,
  output WE_out,
  output [31:0] out_11,
  output [23:0] Address_out,
  output [7:0] out_13,
  output [31:0] out_14,
  output [31:0] out_15,
  output out_16,
  output [3:0] out_17
);

  wire comparator_1_eq;
  wire [31:0] demultiplexer_1_out1;

  Adder adder_1 (.a(node_index), .b(8'h1), .out(out_13));  // open: cin, cout
  Comparator comparator_1 (.a(Address_in[31:24]), .b(node_index), .eq(comparator_1_eq));  // open: gt, lt
  Demultiplexer #(.width(32)) demultiplexer_1 (
    .out0(out_14), .out1(demultiplexer_1_out1), .in(Address_in), .sel(comparator_1_eq));
  Demultiplexer #(.width(32)) demultiplexer_2 (.out0(out_15), .out1(out_11), .in(Data_out), .sel(comparator_1_eq));
  Multiplexer #(.width(32)) multiplexer_1 (.in0(in_7), .in1(in_6), .out(Data_in), .sel(comparator_1_eq));
  Demultiplexer demultiplexer_3 (.out0(out_16), .out1(WE_out), .in(WE), .sel(comparator_1_eq));
  Demultiplexer #(.width(4)) demultiplexer_4 (.out0(out_17), .out1(out_9), .in(Data_size), .sel(comparator_1_eq));
  Bit_Extender #(.in_width(32), .out_width(24), .\type ("zero")) bit_extender_1 (
    .in(demultiplexer_1_out1), .out(Address_out));
endmodule

module screen_driver (
  input  [23:0] in_1,
  input  [31:0] in_2,
  input  in_3,
  output [31:0] out_4,
  output [31:0] out_5,
  output [31:0] out_6,
  output [31:0] out_7,
  output [31:0] out_8,
  output [31:0] out_9,
  output [31:0] out_10,
  output [31:0] out_11,
  output [31:0] out_12,
  output [31:0] out_13,
  output [31:0] out_14,
  output [31:0] out_15,
  output [31:0] out_16,
  output [31:0] out_17,
  output [31:0] out_18,
  output [31:0] out_19,
  output [31:0] out_20,
  output [31:0] out_21,
  output [31:0] out_22,
  output [31:0] out_23,
  output [31:0] out_24,
  output [31:0] out_25,
  output [31:0] out_26,
  output [31:0] out_27,
  output [31:0] out_28,
  output [31:0] out_29,
  output [31:0] out_30,
  output [31:0] out_31,
  output [31:0] out_32,
  output [31:0] out_33,
  output [31:0] out_34,
  output [31:0] out_35
);

  wire and_1_out, and_2_out, decoder_1_out0, decoder_1_out1, decoder_1_out2, decoder_1_out3, decoder_1_out4,
       decoder_1_out5, decoder_1_out6, decoder_1_out7, decoder_1_out8, decoder_1_out9, decoder_1_out10,
       decoder_1_out11, decoder_1_out12, decoder_1_out13, decoder_1_out14, decoder_1_out15, decoder_1_out16,
       decoder_1_out17, decoder_1_out18, decoder_1_out19, decoder_1_out20, decoder_1_out21, decoder_1_out22,
       decoder_1_out23, decoder_1_out24, decoder_1_out25, decoder_1_out26, decoder_1_out27, decoder_1_out28,
       decoder_1_out29, decoder_1_out30, decoder_1_out31, decoder_2_out0, decoder_2_out1, not_1_out;
  wire [31:0] register_1_q, register_2_q, register_3_q, register_4_q, register_5_q, register_6_q,
       register_7_q, register_8_q, register_9_q, register_10_q, register_11_q, register_12_q, register_13_q,
       register_14_q, register_15_q, register_16_q, register_17_q, register_18_q, register_19_q,
       register_20_q, register_21_q, register_22_q, register_23_q, register_24_q, register_25_q,
       register_26_q, register_27_q, register_28_q, register_29_q, register_30_q, register_31_q,
       register_32_q;

  Decoder #(.select(5)) decoder_1 (
    .out0(decoder_1_out0), .out1(decoder_1_out1), .out2(decoder_1_out2), .out3(decoder_1_out3),
    .out4(decoder_1_out4), .out5(decoder_1_out5), .out6(decoder_1_out6), .out7(decoder_1_out7),
    .out8(decoder_1_out8), .out9(decoder_1_out9), .out10(decoder_1_out10), .out11(decoder_1_out11),
    .out12(decoder_1_out12), .out13(decoder_1_out13), .out14(decoder_1_out14), .out15(decoder_1_out15),
    .out16(decoder_1_out16), .out17(decoder_1_out17), .out18(decoder_1_out18), .out19(decoder_1_out19),
    .out20(decoder_1_out20), .out21(decoder_1_out21), .out22(decoder_1_out22), .out23(decoder_1_out23),
    .out24(decoder_1_out24), .out25(decoder_1_out25), .out26(decoder_1_out26), .out27(decoder_1_out27),
    .out28(decoder_1_out28), .out29(decoder_1_out29), .out30(decoder_1_out30), .out31(decoder_1_out31),
    .sel(in_1[4:0]), .en(and_1_out));
  and and_1 (and_1_out, not_1_out, in_3);
  not not_1 (not_1_out, in_1[5]);
  Register #(.width(32)) register_1 (
    .D(in_2), .Q(register_1_q), .clk(decoder_1_out0), .clr(decoder_2_out1));  // open: en
  Register #(.width(32)) register_2 (
    .D(in_2), .Q(register_2_q), .clk(decoder_1_out1), .clr(decoder_2_out1));  // open: en
  Register #(.width(32)) register_3 (
    .D(in_2), .Q(register_3_q), .clk(decoder_1_out2), .clr(decoder_2_out1));  // open: en
  Register #(.width(32)) register_4 (
    .D(in_2), .Q(register_4_q), .clk(decoder_1_out3), .clr(decoder_2_out1));  // open: en
  Register #(.width(32)) register_5 (
    .D(in_2), .Q(register_5_q), .clk(decoder_1_out4), .clr(decoder_2_out1));  // open: en
  Register #(.width(32)) register_6 (
    .D(in_2), .Q(register_6_q), .clk(decoder_1_out5), .clr(decoder_2_out1));  // open: en
  Register #(.width(32)) register_7 (
    .D(in_2), .Q(register_7_q), .clk(decoder_1_out6), .clr(decoder_2_out1));  // open: en
  Register #(.width(32)) register_8 (
    .D(in_2), .Q(register_8_q), .clk(decoder_1_out7), .clr(decoder_2_out1));  // open: en
  Register #(.width(32)) register_9 (
    .D(in_2), .Q(register_9_q), .clk(decoder_1_out8), .clr(decoder_2_out1));  // open: en
  Register #(.width(32)) register_10 (
    .D(in_2), .Q(register_10_q), .clk(decoder_1_out9), .clr(decoder_2_out1));  // open: en
  Register #(.width(32)) register_11 (
    .D(in_2), .Q(register_11_q), .clk(decoder_1_out10), .clr(decoder_2_out1));  // open: en
  Register #(.width(32)) register_12 (
    .D(in_2), .Q(register_12_q), .clk(decoder_1_out11), .clr(decoder_2_out1));  // open: en
  Register #(.width(32)) register_13 (
    .D(in_2), .Q(register_13_q), .clk(decoder_1_out12), .clr(decoder_2_out1));  // open: en
  Register #(.width(32)) register_14 (
    .D(in_2), .Q(register_14_q), .clk(decoder_1_out13), .clr(decoder_2_out1));  // open: en
  Register #(.width(32)) register_15 (
    .D(in_2), .Q(register_15_q), .clk(decoder_1_out14), .clr(decoder_2_out1));  // open: en
  Register #(.width(32)) register_16 (
    .D(in_2), .Q(register_16_q), .clk(decoder_1_out15), .clr(decoder_2_out1));  // open: en
  Register #(.width(32)) register_17 (
    .D(in_2), .Q(register_17_q), .clk(decoder_1_out16), .clr(decoder_2_out1));  // open: en
  Register #(.width(32)) register_18 (
    .D(in_2), .Q(register_18_q), .clk(decoder_1_out17), .clr(decoder_2_out1));  // open: en
  Register #(.width(32)) register_19 (
    .D(in_2), .Q(register_19_q), .clk(decoder_1_out18), .clr(decoder_2_out1));  // open: en
  Register #(.width(32)) register_20 (
    .D(in_2), .Q(register_20_q), .clk(decoder_1_out19), .clr(decoder_2_out1));  // open: en
  Register #(.width(32)) register_21 (
    .D(in_2), .Q(register_21_q), .clk(decoder_1_out20), .clr(decoder_2_out1));  // open: en
  Register #(.width(32)) register_22 (
    .D(in_2), .Q(register_22_q), .clk(decoder_1_out21), .clr(decoder_2_out1));  // open: en
  Register #(.width(32)) register_23 (
    .D(in_2), .Q(register_23_q), .clk(decoder_1_out22), .clr(decoder_2_out1));  // open: en
  Register #(.width(32)) register_24 (
    .D(in_2), .Q(register_24_q), .clk(decoder_1_out23), .clr(decoder_2_out1));  // open: en
  Register #(.width(32)) register_25 (
    .D(in_2), .Q(register_25_q), .clk(decoder_1_out24), .clr(decoder_2_out1));  // open: en
  Register #(.width(32)) register_26 (
    .D(in_2), .Q(register_26_q), .clk(decoder_1_out25), .clr(decoder_2_out1));  // open: en
  Register #(.width(32)) register_27 (
    .D(in_2), .Q(register_27_q), .clk(decoder_1_out26), .clr(decoder_2_out1));  // open: en
  Register #(.width(32)) register_28 (
    .D(in_2), .Q(register_28_q), .clk(decoder_1_out27), .clr(decoder_2_out1));  // open: en
  Register #(.width(32)) register_29 (
    .D(in_2), .Q(register_29_q), .clk(decoder_1_out28), .clr(decoder_2_out1));  // open: en
  Register #(.width(32)) register_30 (
    .D(in_2), .Q(register_30_q), .clk(decoder_1_out29), .clr(decoder_2_out1));  // open: en
  Register #(.width(32)) register_31 (
    .D(in_2), .Q(register_31_q), .clk(decoder_1_out30), .clr(decoder_2_out1));  // open: en
  Register #(.width(32)) register_32 (
    .D(in_2), .Q(register_32_q), .clk(decoder_1_out31), .clr(decoder_2_out1));  // open: en
  and and_2 (and_2_out, in_1[5], in_3);
  Register #(.width(32)) register_33 (
    .D(register_1_q), .Q(out_4), .clk(decoder_2_out1), .clr(decoder_2_out0));  // open: en
  Register #(.width(32)) register_34 (
    .D(register_2_q), .Q(out_5), .clk(decoder_2_out1), .clr(decoder_2_out0));  // open: en
  Register #(.width(32)) register_35 (
    .D(register_3_q), .Q(out_6), .clk(decoder_2_out1), .clr(decoder_2_out0));  // open: en
  Register #(.width(32)) register_36 (
    .D(register_4_q), .Q(out_7), .clk(decoder_2_out1), .clr(decoder_2_out0));  // open: en
  Register #(.width(32)) register_37 (
    .D(register_5_q), .Q(out_8), .clk(decoder_2_out1), .clr(decoder_2_out0));  // open: en
  Register #(.width(32)) register_38 (
    .D(register_6_q), .Q(out_9), .clk(decoder_2_out1), .clr(decoder_2_out0));  // open: en
  Register #(.width(32)) register_39 (
    .D(register_7_q), .Q(out_10), .clk(decoder_2_out1), .clr(decoder_2_out0));  // open: en
  Register #(.width(32)) register_40 (
    .D(register_8_q), .Q(out_11), .clk(decoder_2_out1), .clr(decoder_2_out0));  // open: en
  Register #(.width(32)) register_41 (
    .D(register_9_q), .Q(out_12), .clk(decoder_2_out1), .clr(decoder_2_out0));  // open: en
  Register #(.width(32)) register_42 (
    .D(register_10_q), .Q(out_13), .clk(decoder_2_out1), .clr(decoder_2_out0));  // open: en
  Register #(.width(32)) register_43 (
    .D(register_11_q), .Q(out_14), .clk(decoder_2_out1), .clr(decoder_2_out0));  // open: en
  Register #(.width(32)) register_44 (
    .D(register_12_q), .Q(out_15), .clk(decoder_2_out1), .clr(decoder_2_out0));  // open: en
  Register #(.width(32)) register_45 (
    .D(register_13_q), .Q(out_16), .clk(decoder_2_out1), .clr(decoder_2_out0));  // open: en
  Register #(.width(32)) register_46 (
    .D(register_14_q), .Q(out_17), .clk(decoder_2_out1), .clr(decoder_2_out0));  // open: en
  Register #(.width(32)) register_47 (
    .D(register_15_q), .Q(out_18), .clk(decoder_2_out1), .clr(decoder_2_out0));  // open: en
  Register #(.width(32)) register_48 (
    .D(register_16_q), .Q(out_19), .clk(decoder_2_out1), .clr(decoder_2_out0));  // open: en
  Register #(.width(32)) register_49 (
    .D(register_17_q), .Q(out_20), .clk(decoder_2_out1), .clr(decoder_2_out0));  // open: en
  Register #(.width(32)) register_50 (
    .D(register_18_q), .Q(out_21), .clk(decoder_2_out1), .clr(decoder_2_out0));  // open: en
  Register #(.width(32)) register_51 (
    .D(register_19_q), .Q(out_22), .clk(decoder_2_out1), .clr(decoder_2_out0));  // open: en
  Register #(.width(32)) register_52 (
    .D(register_20_q), .Q(out_23), .clk(decoder_2_out1), .clr(decoder_2_out0));  // open: en
  Register #(.width(32)) register_53 (
    .D(register_21_q), .Q(out_24), .clk(decoder_2_out1), .clr(decoder_2_out0));  // open: en
  Register #(.width(32)) register_54 (
    .D(register_22_q), .Q(out_25), .clk(decoder_2_out1), .clr(decoder_2_out0));  // open: en
  Register #(.width(32)) register_55 (
    .D(register_23_q), .Q(out_26), .clk(decoder_2_out1), .clr(decoder_2_out0));  // open: en
  Register #(.width(32)) register_56 (
    .D(register_24_q), .Q(out_27), .clk(decoder_2_out1), .clr(decoder_2_out0));  // open: en
  Register #(.width(32)) register_57 (
    .D(register_25_q), .Q(out_28), .clk(decoder_2_out1), .clr(decoder_2_out0));  // open: en
  Register #(.width(32)) register_58 (
    .D(register_26_q), .Q(out_29), .clk(decoder_2_out1), .clr(decoder_2_out0));  // open: en
  Register #(.width(32)) register_59 (
    .D(register_27_q), .Q(out_30), .clk(decoder_2_out1), .clr(decoder_2_out0));  // open: en
  Register #(.width(32)) register_60 (
    .D(register_28_q), .Q(out_31), .clk(decoder_2_out1), .clr(decoder_2_out0));  // open: en
  Register #(.width(32)) register_61 (
    .D(register_29_q), .Q(out_32), .clk(decoder_2_out1), .clr(decoder_2_out0));  // open: en
  Register #(.width(32)) register_62 (
    .D(register_30_q), .Q(out_33), .clk(decoder_2_out1), .clr(decoder_2_out0));  // open: en
  Register #(.width(32)) register_63 (
    .D(register_31_q), .Q(out_34), .clk(decoder_2_out1), .clr(decoder_2_out0));  // open: en
  Register #(.width(32)) register_64 (
    .D(register_32_q), .Q(out_35), .clk(decoder_2_out1), .clr(decoder_2_out0));  // open: en
  Decoder decoder_2 (.out0(decoder_2_out0), .out1(decoder_2_out1), .sel(in_1[0]), .en(and_2_out));
endmodule
